// Logisim project L0_CRC_3.circ as structural Verilog: 2 circuits, main circuit CRC
module CRC (
  input  [7:0] A,
  input  [3:0] B,
  output [10:0] out_3
);

  wire [7:0] \除法器_6_aaa ;
  wire [10:0] A_t, B_t, bit_extender_1_out, bit_extender_2_out, \除法器_1_aaa , \除法器_2_aaa , \除法器_3_aaa ,
       \除法器_4_aaa , \除法器_5_aaa , \除法器_7_aaa , \除法器_8_aaa ;

  assign bit_extender_1_out = {{7{1'b0}}, B};  // Bit_Extender bit_extender_1
  // Probe on B_t
  // Probe on A_t
  assign bit_extender_2_out = {{3{1'b0}}, A};  // Bit_Extender bit_extender_2
  Shifter #(.width(11)) shifter_1 (.in(bit_extender_1_out), .\dist (4'b0111), .out(B_t));
  Shifter #(.width(11)) shifter_2 (.in(bit_extender_2_out), .\dist (4'b0011), .out(A_t));
  \除法器  \u_除法器_1  (.A(A_t), .B(B_t), .AAA(\除法器_1_aaa ));
  \除法器  \u_除法器_2  (.A(\除法器_8_aaa ), .B(B_t), .AAA(\除法器_2_aaa ));
  \除法器  \u_除法器_3  (.A(\除法器_1_aaa ), .B(B_t), .AAA(\除法器_3_aaa ));
  \除法器  \u_除法器_4  (.A(\除法器_2_aaa ), .B(B_t), .AAA(\除法器_4_aaa ));
  \除法器  \u_除法器_5  (.A(\除法器_3_aaa ), .B(B_t), .AAA(\除法器_5_aaa ));
  \除法器  \u_除法器_6  (.A(\除法器_4_aaa ), .B(B_t), .AAA({out_3[2:0], \除法器_6_aaa }));
  \除法器  \u_除法器_7  (.A(\除法器_5_aaa ), .B(B_t), .AAA(\除法器_7_aaa ));
  \除法器  \u_除法器_8  (.A(\除法器_7_aaa ), .B(B_t), .AAA(\除法器_8_aaa ));
  // Probe on out_3[2:0]
  // Probe on out_3[2:0]

  assign out_3[10:3] = A;
endmodule

module \除法器  (
  input  [10:0] A,
  input  [10:0] B,
  output [10:0] AAA
);

  wire comparator_1_lt;
  wire [10:0] multiplexer_1_out, xor_1_out;

  // Probe on A
  // Probe on xor_1_out
  assign xor_1_out = A ^ B;  // XOR_Gate xor_1, 11 bits wide
  Multiplexer #(.width(11)) multiplexer_1 (
    .in0(A), .in1(xor_1_out), .out(multiplexer_1_out), .sel(comparator_1_lt));  // open: en
  Comparator #(.width(11), .mode("unsigned")) comparator_1 (
    .a(xor_1_out), .b(11'h400), .lt(comparator_1_lt));  // open: gt, eq
  Shifter #(.width(11)) shifter_1 (.in(multiplexer_1_out), .\dist (4'b0001), .out(AAA));
endmodule
