// Logisim project L0_FSM_3.circ as structural Verilog: 3 circuits, main circuit fsm
module fsm (
  input  [1:0] in,
  input  clr,
  output z
);

  wire clock_1_out, counter_1_q, counter_2_q, not_1_out;
  wire [1:0] multiplexer_1_out, register_1_q, \状态转换_1_c_ ;

  Counter #(.width(1), .max('h1), .ongoal("stay")) counter_1 (
    .Q(counter_1_q), .clk(clock_1_out), .clr(counter_2_q));  // open: load, D, count, carry
  Multiplexer #(.width(2)) multiplexer_1 (
    .in0(2'b00), .in1(register_1_q), .out(multiplexer_1_out), .sel(counter_1_q));  // open: en
  // Probe on multiplexer_1_out
  \状态转换  \u_状态转换_1  (.c(multiplexer_1_out), .in(in), .c_(\状态转换_1_c_ ));
  // Probe on \状态转换_1_c_ 
  Clock clock_1 (.out(clock_1_out));
  Register #(.width(2)) register_1 (
    .D(\状态转换_1_c_ ), .Q(register_1_q), .clk(clock_1_out), .clr(counter_2_q));  // open: en
  // Probe on register_1_q
  not not_1 (not_1_out, clr);
  Counter #(.width(1), .max('h1)) counter_2 (
    .Q(counter_2_q), .clk(clock_1_out), .clr(not_1_out));  // open: load, D, count, carry
  \输出逻辑  \u_输出逻辑_1  (.c(register_1_q), .in(in), .z(z));
endmodule

module \状态转换  (
  input  [1:0] c,
  input  [1:0] in,
  output [1:0] c_
);

  wire and_1_out, and_2_out, and_3_out, and_4_out, and_5_out, not_1_out, not_2_out, not_3_out, not_4_out,
       not_5_out, not_6_out, not_7_out, not_8_out, not_9_out;

  not not_1 (not_1_out, c[1]);
  not not_2 (not_2_out, in[0]);
  not not_3 (not_3_out, c[0]);
  not not_4 (not_4_out, in[0]);
  not not_5 (not_5_out, c[1]);
  not not_6 (not_6_out, in[1]);
  not not_7 (not_7_out, in[1]);
  not not_8 (not_8_out, c[0]);
  not not_9 (not_9_out, in[0]);
  and and_1 (and_1_out, not_1_out, c[0], not_2_out);
  and and_2 (and_2_out, c[1], not_3_out, not_4_out);
  and and_3 (and_3_out, not_5_out, not_6_out, in[0]);
  and and_4 (and_4_out, c[0], not_7_out, in[0]);
  and and_5 (and_5_out, c[1], not_8_out, not_9_out);
  or or_1 (c_[1], and_1_out, and_2_out);
  or or_2 (c_[0], and_3_out, and_4_out, and_5_out);
endmodule

module \输出逻辑  (
  input  [1:0] c,
  input  [1:0] in,
  output z
);

  wire not_1_out, not_2_out;

  not not_1 (not_1_out, c[0]);
  not not_2 (not_2_out, in[0]);
  and and_1 (z, c[1], not_1_out, not_2_out);
endmodule
