// Logisim project L0_GRF_1.circ as structural Verilog: 1 circuit, main circuit grf
module grf (
  input  in_1,
  input  in_2,
  input  in_3,
  input  [31:0] WD,
  input  [4:0] A1,
  input  [4:0] A3,
  input  [4:0] A2,
  output [31:0] RD2,
  output [31:0] RD1
);

  wire undriven;
  wire [31:0] _0, _1, _2, _3, _4, _5, _6, _7, _8, _9, _10, _11, _12, _13, _14, _15, _16, _17, _18, _19, _20,
       _21, _22, _23, _24, _25, _26, _27, _28, _29, _30, _31, demultiplexer_1_out1, demultiplexer_1_out2,
       demultiplexer_1_out3, demultiplexer_1_out4, demultiplexer_1_out5, demultiplexer_1_out6,
       demultiplexer_1_out7, demultiplexer_1_out8, demultiplexer_1_out9, demultiplexer_1_out10,
       demultiplexer_1_out11, demultiplexer_1_out12, demultiplexer_1_out13, demultiplexer_1_out14,
       demultiplexer_1_out15, demultiplexer_1_out16, demultiplexer_1_out17, demultiplexer_1_out18,
       demultiplexer_1_out19, demultiplexer_1_out20, demultiplexer_1_out21, demultiplexer_1_out22,
       demultiplexer_1_out23, demultiplexer_1_out24, demultiplexer_1_out25, demultiplexer_1_out26,
       demultiplexer_1_out27, demultiplexer_1_out28, demultiplexer_1_out29, demultiplexer_1_out30,
       demultiplexer_1_out31;

  Multiplexer multiplexer_1 (.in0(1'b0), .sel(in_3));  // open: in1, out, en
  Demultiplexer #(.select(5), .width(32), .tristate("true")) demultiplexer_1 (
    .out1(demultiplexer_1_out1), .out2(demultiplexer_1_out2), .out3(demultiplexer_1_out3),
    .out4(demultiplexer_1_out4), .out5(demultiplexer_1_out5), .out6(demultiplexer_1_out6),
    .out7(demultiplexer_1_out7), .out8(demultiplexer_1_out8), .out9(demultiplexer_1_out9),
    .out10(demultiplexer_1_out10), .out11(demultiplexer_1_out11), .out12(demultiplexer_1_out12),
    .out13(demultiplexer_1_out13), .out14(demultiplexer_1_out14), .out15(demultiplexer_1_out15),
    .out16(demultiplexer_1_out16), .out17(demultiplexer_1_out17), .out18(demultiplexer_1_out18),
    .out19(demultiplexer_1_out19), .out20(demultiplexer_1_out20), .out21(demultiplexer_1_out21),
    .out22(demultiplexer_1_out22), .out23(demultiplexer_1_out23), .out24(demultiplexer_1_out24),
    .out25(demultiplexer_1_out25), .out26(demultiplexer_1_out26), .out27(demultiplexer_1_out27),
    .out28(demultiplexer_1_out28), .out29(demultiplexer_1_out29), .out30(demultiplexer_1_out30),
    .out31(demultiplexer_1_out31), .in(WD), .sel(A3), .en(in_3));  // open: out0
  Register #(.width(32)) u__0 (.D({32{1'b0}}), .Q(_0), .clk(in_1), .clr(in_2));  // open: en
  Register #(.width(32)) u__4 (.D(demultiplexer_1_out4), .Q(_4), .clk(in_1), .clr(in_2));  // open: en
  Register #(.width(32)) u__8 (.D(demultiplexer_1_out8), .Q(_8), .clk(in_1), .clr(in_2));  // open: en
  Register #(.width(32)) u__12 (.D(demultiplexer_1_out12), .Q(_12), .clk(in_1), .clr(in_2));  // open: en
  Register #(.width(32)) u__16 (.D(demultiplexer_1_out16), .Q(_16), .clk(in_1), .clr(in_2));  // open: en
  Register #(.width(32)) u__20 (.D(demultiplexer_1_out20), .Q(_20), .clk(in_1), .clr(in_2));  // open: en
  Register #(.width(32)) u__24 (.D(demultiplexer_1_out24), .Q(_24), .clk(in_1), .clr(in_2));  // open: en
  Register #(.width(32)) u__28 (.D(demultiplexer_1_out28), .Q(_28), .clk(in_1), .clr(in_2));  // open: en
  Register #(.width(32)) u__5 (.D(demultiplexer_1_out5), .Q(_5), .clk(in_1), .clr(in_2));  // open: en
  Register #(.width(32)) u__1 (.D(demultiplexer_1_out1), .Q(_1), .clk(in_1), .clr(in_2));  // open: en
  Register #(.width(32)) u__9 (.D(demultiplexer_1_out9), .Q(_9), .clk(in_1), .clr(in_2));  // open: en
  Register #(.width(32)) u__13 (.D(demultiplexer_1_out13), .Q(_13), .clk(in_1), .clr(in_2));  // open: en
  Register #(.width(32)) u__17 (.D(demultiplexer_1_out17), .Q(_17), .clk(in_1), .clr(in_2));  // open: en
  Register #(.width(32)) u__21 (.D(demultiplexer_1_out21), .Q(_21), .clk(in_1), .clr(in_2));  // open: en
  Register #(.width(32)) u__25 (.D(demultiplexer_1_out25), .Q(_25), .clk(in_1), .clr(in_2));  // open: en
  Register #(.width(32)) u__29 (.D(demultiplexer_1_out29), .Q(_29), .clk(in_1), .clr(in_2));  // open: en
  Register #(.width(32)) u__2 (.D(demultiplexer_1_out2), .Q(_2), .clk(in_1), .clr(in_2));  // open: en
  Register #(.width(32)) u__6 (.D(demultiplexer_1_out6), .Q(_6), .clk(in_1), .clr(in_2));  // open: en
  Register #(.width(32)) u__10 (.D(demultiplexer_1_out10), .Q(_10), .clk(in_1), .clr(in_2));  // open: en
  Register #(.width(32)) u__14 (.D(demultiplexer_1_out14), .Q(_14), .clk(in_1), .clr(in_2));  // open: en
  Register #(.width(32)) u__18 (.D(demultiplexer_1_out18), .Q(_18), .clk(in_1), .clr(in_2));  // open: en
  Register #(.width(32)) u__22 (.D(demultiplexer_1_out22), .Q(_22), .clk(in_1), .clr(in_2));  // open: en
  Register #(.width(32)) u__26 (.D(demultiplexer_1_out26), .Q(_26), .clk(in_1), .clr(in_2));  // open: en
  Register #(.width(32)) u__30 (.D(demultiplexer_1_out30), .Q(_30), .clk(in_1), .clr(in_2));  // open: en
  Register #(.width(32)) u__3 (.D(demultiplexer_1_out3), .Q(_3), .clk(in_1), .clr(in_2));  // open: en
  Register #(.width(32)) u__7 (.D(demultiplexer_1_out7), .Q(_7), .clk(in_1), .clr(in_2));  // open: en
  Register #(.width(32)) u__11 (.D(demultiplexer_1_out11), .Q(_11), .clk(in_1), .clr(in_2));  // open: en
  Register #(.width(32)) u__15 (.D(demultiplexer_1_out15), .Q(_15), .clk(in_1), .clr(in_2));  // open: en
  Register #(.width(32)) u__19 (.D(demultiplexer_1_out19), .Q(_19), .clk(in_1), .clr(in_2));  // open: en
  Register #(.width(32)) u__23 (.D(demultiplexer_1_out23), .Q(_23), .clk(in_1), .clr(in_2));  // open: en
  Register #(.width(32)) u__27 (.D(demultiplexer_1_out27), .Q(_27), .clk(in_1), .clr(in_2));  // open: en
  Register #(.width(32)) u__31 (.D(demultiplexer_1_out31), .Q(_31), .clk(in_1), .clr(in_2));  // open: en
  Multiplexer #(.select(5), .width(32)) multiplexer_2 (
    .in0(_0), .in1(_1), .in2(_2), .in3(_3), .in4(_4), .in5(_5), .in6(_6), .in7(_7), .in8(_8), .in9(_9),
    .in10(_10), .in11(_11), .in12(_12), .in13(_13), .in14(_14), .in15(_15), .in16(_16), .in17(_17),
    .in18(_18), .in19(_19), .in20(_20), .in21(_21), .in22(_22), .in23(_23), .in24(_24), .in25(_25),
    .in26(_26), .in27(_27), .in28(_28), .in29(_29), .in30(_30), .in31(_31), .out(RD1), .sel(A1), .en(undriven));
  Multiplexer #(.select(5), .width(32)) multiplexer_3 (
    .in0(_0), .in1(_1), .in2(_2), .in3(_3), .in4(_4), .in5(_5), .in6(_6), .in7(_7), .in8(_8), .in9(_9),
    .in10(_10), .in11(_11), .in12(_12), .in13(_13), .in14(_14), .in15(_15), .in16(_16), .in17(_17),
    .in18(_18), .in19(_19), .in20(_20), .in21(_21), .in22(_22), .in23(_23), .in24(_24), .in25(_25),
    .in26(_26), .in27(_27), .in28(_28), .in29(_29), .in30(_30), .in31(_31), .out(RD2), .sel(A2));  // open: en

  // Other names for the same wires on the sheet: clk = in_1; reset = in_2; we = in_3
endmodule
