// Logisim project L1_navigation_2020_1.circ as structural Verilog: 3 circuits, main circuit navigation
module navigation (
  input  [1:0] dir,
  input  in_2,
  input  in_3,
  output arrive,
  output hit
);

  wire counter_1_q;
  wire [3:0] multiplexer_1_out, register_1_q, \状态转换_out_3 ;

  Multiplexer #(.width(4)) multiplexer_1 (
    .in0(4'b0000), .in1(register_1_q), .out(multiplexer_1_out), .sel(counter_1_q));  // open: en
  Counter #(.width(1), .max('h1), .ongoal("stay")) counter_1 (
    .Q(counter_1_q), .clk(in_3));  // open: load, D, count, carry, clr
  \状态转换  \u_状态转换  (.dir(dir), .out_3(\状态转换_out_3 ), .C(multiplexer_1_out));
  Register #(.width(4)) register_1 (.D(\状态转换_out_3 ), .Q(register_1_q), .clk(in_3), .clr(in_2));  // open: en
  \输出  \u_输出_1  (.C(register_1_q), .arrive(arrive), .hit(hit));

  // Other names for the same wires on the sheet: clk = in_3; reset = in_2
endmodule

module \状态转换  (
  input  [3:0] C,
  input  [1:0] dir,
  output [3:0] out_3
);

  wire and_1_out, and_2_out, and_3_out, and_4_out, and_5_out, and_6_out, and_7_out, and_8_out, and_9_out,
       and_10_out, and_11_out, and_12_out, and_13_out, and_14_out, and_15_out, and_16_out, not_1_out,
       not_2_out, not_3_out, not_4_out, not_5_out, not_6_out, not_7_out, not_8_out, not_9_out, not_10_out,
       not_11_out, not_12_out, not_13_out, not_14_out, not_15_out, not_16_out, not_17_out, not_18_out,
       not_19_out, not_20_out, not_21_out, not_22_out, not_23_out, not_24_out, not_25_out, not_26_out,
       not_27_out, not_28_out, not_29_out, not_30_out, not_31_out, not_32_out, not_33_out, not_34_out,
       not_35_out, not_36_out, not_37_out, not_38_out, not_39_out, not_40_out;

  not not_1 (not_1_out, C[3]);
  not not_2 (not_2_out, C[1]);
  not not_3 (not_3_out, dir[1]);
  not not_4 (not_4_out, dir[0]);
  not not_5 (not_5_out, C[3]);
  not not_6 (not_6_out, dir[1]);
  not not_7 (not_7_out, C[3]);
  not not_8 (not_8_out, C[2]);
  not not_9 (not_9_out, dir[1]);
  not not_10 (not_10_out, C[3]);
  not not_11 (not_11_out, dir[1]);
  not not_12 (not_12_out, dir[0]);
  not not_13 (not_13_out, C[3]);
  not not_14 (not_14_out, C[1]);
  not not_15 (not_15_out, dir[1]);
  not not_16 (not_16_out, C[3]);
  not not_17 (not_17_out, C[1]);
  not not_18 (not_18_out, dir[0]);
  not not_19 (not_19_out, C[3]);
  not not_20 (not_20_out, C[3]);
  not not_21 (not_21_out, C[2]);
  not not_22 (not_22_out, dir[1]);
  not not_23 (not_23_out, dir[0]);
  not not_24 (not_24_out, C[3]);
  not not_25 (not_25_out, C[3]);
  not not_26 (not_26_out, C[3]);
  not not_27 (not_27_out, dir[0]);
  not not_28 (not_28_out, C[3]);
  not not_29 (not_29_out, C[1]);
  not not_30 (not_30_out, dir[1]);
  not not_31 (not_31_out, C[3]);
  not not_32 (not_32_out, C[2]);
  not not_33 (not_33_out, C[1]);
  not not_34 (not_34_out, C[3]);
  not not_35 (not_35_out, C[1]);
  not not_36 (not_36_out, dir[0]);
  not not_37 (not_37_out, C[3]);
  not not_38 (not_38_out, C[3]);
  not not_39 (not_39_out, dir[1]);
  not not_40 (not_40_out, dir[0]);
  and and_1 (and_1_out, not_1_out, C[2], not_2_out, not_3_out, not_4_out);
  and and_2 (and_2_out, not_5_out, C[2], C[1], not_6_out, dir[0]);
  and and_3 (and_3_out, not_7_out, not_8_out, C[1], not_9_out);
  and and_4 (and_4_out, not_10_out, C[1], not_11_out, not_12_out);
  and and_5 (and_5_out, not_13_out, C[2], not_14_out, not_15_out, dir[0]);
  and and_6 (and_6_out, not_16_out, C[2], not_17_out, dir[1], not_18_out);
  and and_7 (and_7_out, not_19_out, C[2], C[1], dir[1], dir[0]);
  and and_8 (and_8_out, not_20_out, not_21_out, not_22_out, not_23_out);
  and and_9 (and_9_out, not_24_out, C[1], dir[1], dir[0]);
  and and_10 (and_10_out, not_25_out, C[2], dir[1], dir[0]);
  and and_11 (and_11_out, not_26_out, C[2], C[1], not_27_out);
  and and_12 (and_12_out, not_28_out, not_29_out, not_30_out, dir[0]);
  and and_13 (and_13_out, not_31_out, not_32_out, not_33_out, dir[1]);
  and and_14 (and_14_out, not_34_out, not_35_out, dir[1], not_36_out);
  and and_15 (and_15_out, not_37_out, C[1], dir[1], dir[0]);
  and and_16 (and_16_out, not_38_out, C[2], C[1], not_39_out, not_40_out);
  or or_1 (out_3[3], and_1_out, and_2_out);
  or or_2 (out_3[2], and_3_out, and_4_out, and_5_out, and_6_out, and_7_out);
  or or_3 (out_3[1], and_8_out, and_9_out, and_10_out, and_11_out);
  or or_4 (out_3[0], and_12_out, and_13_out, and_14_out, and_15_out, and_16_out);
endmodule

module \输出  (
  input  [3:0] C,
  output arrive,
  output hit
);

  wire not_1_out, not_2_out, not_3_out, not_4_out;

  not not_1 (not_1_out, C[2]);
  not not_2 (not_2_out, C[1]);
  not not_3 (not_3_out, C[0]);
  not not_4 (not_4_out, C[3]);
  and and_1 (arrive, C[3], not_1_out, not_2_out, not_3_out);
  and and_2 (hit, not_4_out, C[0]);
endmodule
