// Logisim project P5_V1.circ as structural Verilog
module main (
  input  in_1,
  output [31:0] out_2,
  output [31:0] out_3,
  output out_4,
  output [4:0] out_5,
  output [31:0] out_6,
  output out_7,
  output [31:0] out_8,
  output [31:0] out_9
);

  wire ALU_sel, Branch, clk, cmp_1_out_3, ExtOp, Jal_sel, Jr_sel, MemToReg, RegDst, Zero;
  wire [3:0] ALUCtr;
  wire [4:0] splitter_1_a3, splitter_1_rs_a1, splitter_1_rt_a2, splitter_1_shamt;
  wire [5:0] splitter_1_funct, splitter_1_op;
  wire [15:0] splitter_1_offset;
  wire [25:0] splitter_1_instrindex;
  wire [31:0] RD1, ReadData, SignImm, srcbsel_1_out_4;

  // Probe on out_2
  // Probe on out_3
  Clock clock_1 (.out(clk));
  IFU ifu_1 (
    .Zero(Zero), .Branch(Branch), .clk(clk), .reset(in_1), .SignImm(SignImm), .RD1(RD1),
    .in_2(splitter_1_instrindex), .JalSrc(Jal_sel), .pc(out_3), .Instr(out_2), .JRSrc(Jr_sel));
  choose choose_1 ();
  \流水线寄存器  \u_流水线寄存器_1  ();
  Splitter splitter_1 (
    .in_1(out_2), .offset(splitter_1_offset), .Rs_A1(splitter_1_rs_a1), .op(splitter_1_op),
    .Rt_A2(splitter_1_rt_a2), .A3(splitter_1_a3), .funct(splitter_1_funct), .shamt(splitter_1_shamt),
    .InstrIndex(splitter_1_instrindex));
  Controller controller_1 (
    .funct(splitter_1_funct), .op(splitter_1_op), .out_3(RegDst), .out_4(ALU_sel), .out_5(MemToReg),
    .out_6(out_4), .out_7(out_7), .out_8(Branch), .out_9(ExtOp), .out_12(ALUCtr), .out_10(Jr_sel),
    .jal(Jal_sel));
  // Probe on splitter_1_rs_a1
  A3sel a3sel_1 (.A3_in(splitter_1_a3), .Jalsrc(Jal_sel), .add(out_5), .A2(splitter_1_rt_a2), .RegDst(RegDst));
  WD3sel wd3sel_1 (
    .ALUResult(out_8), .ReadData(ReadData), .pc(out_3), .JalSrc(Jal_sel), .MemToReg(MemToReg), .regdata(out_6));
  EXT ext_1 (.offset(splitter_1_offset), .ExtOp(ExtOp), .SignImm(SignImm));
  \转发  \u_转发_1  ();
  GRF grf_1 (
    .in_1(clk), .in_2(in_1), .in_3(out_4), .WD(out_6), .A3(out_5), .RD2(out_9), .RD1(RD1),
    .A1(splitter_1_rs_a1), .A2(splitter_1_rt_a2));
  CMP cmp_1 (.in_1(RD1), .in_2(out_9), .out_3(cmp_1_out_3));
  choose choose_2 ();
  \流水线寄存器  \u_流水线寄存器_2  ();
  \转发  \u_转发_2  ();
  A3sel A3_Sel ();  // open: A3_in, Jalsrc, add, A2, RegDst
  choose choose_3 ();
  SrcBsel srcbsel_1 (.in_1(out_9), .in_2(SignImm), .in_3(ALU_sel), .out_4(srcbsel_1_out_4));
  ALU alu_1 (.in_1(ALUCtr), .in_2(RD1), .in_3(srcbsel_1_out_4), .out_5(out_8), .Zero(Zero), .in_4(splitter_1_shamt));
  \流水线寄存器  \u_流水线寄存器_3  ();
  choose choose_4 ();
  \转发  \u_转发_3  ();
  DM dm_1 (.ALUResult(out_8), .WriteData(out_9), .MemWrite(out_7), .out_6(ReadData), .reset(in_1), .clk(clk));
  choose choose_5 ();
  \流水线寄存器  \u_流水线寄存器_4  ();
  WD3sel wd3sel_2 (
    .ALUResult(out_8), .ReadData(ReadData), .pc(out_3), .JalSrc(Jal_sel), .MemToReg(MemToReg), .regdata(out_6));
  \转发  \u_转发_4  ();

  // Other names for the same wires on the sheet: Instr[31:0] = out_2; MemAddr[31:0] = out_8; MemWrite = out_7;
  //   pc[31:0] = out_3; MemData[31:0] = out_9; RD2[31:0] = out_9; RegAddr[4:0] = out_5; RegData[31:0] = out_6;
  //   RegWrite = out_4; reset = in_1

  // Notes on the sheet:
  //   选A3
  //   选SrcB
  //   这里做jal=E_PC+4的选择
  //   选RegData
endmodule

module GRF (
  input  in_1,
  input  in_2,
  input  in_3,
  input  [31:0] WD,
  input  [4:0] A1,
  input  [4:0] A3,
  input  [4:0] A2,
  output [31:0] RD2,
  output [31:0] RD1
);

  wire undriven;
  wire [31:0] _0, _1, _2, _3, _4, _5, _6, _7, _8, _9, _10, _11, _12, _13, _14, _15, _16, _17, _18, _19, _20,
       _21, _22, _23, _24, _25, _26, _27, _28, _29, _30, _31, demultiplexer_1_out1, demultiplexer_1_out2,
       demultiplexer_1_out3, demultiplexer_1_out4, demultiplexer_1_out5, demultiplexer_1_out6,
       demultiplexer_1_out7, demultiplexer_1_out8, demultiplexer_1_out9, demultiplexer_1_out10,
       demultiplexer_1_out11, demultiplexer_1_out12, demultiplexer_1_out13, demultiplexer_1_out14,
       demultiplexer_1_out15, demultiplexer_1_out16, demultiplexer_1_out17, demultiplexer_1_out18,
       demultiplexer_1_out19, demultiplexer_1_out20, demultiplexer_1_out21, demultiplexer_1_out22,
       demultiplexer_1_out23, demultiplexer_1_out24, demultiplexer_1_out25, demultiplexer_1_out26,
       demultiplexer_1_out27, demultiplexer_1_out28, demultiplexer_1_out29, demultiplexer_1_out30,
       demultiplexer_1_out31;

  Demultiplexer #(.select(5), .width(32), .tristate("true")) demultiplexer_1 (
    .out1(demultiplexer_1_out1), .out2(demultiplexer_1_out2), .out3(demultiplexer_1_out3),
    .out4(demultiplexer_1_out4), .out5(demultiplexer_1_out5), .out6(demultiplexer_1_out6),
    .out7(demultiplexer_1_out7), .out8(demultiplexer_1_out8), .out9(demultiplexer_1_out9),
    .out10(demultiplexer_1_out10), .out11(demultiplexer_1_out11), .out12(demultiplexer_1_out12),
    .out13(demultiplexer_1_out13), .out14(demultiplexer_1_out14), .out15(demultiplexer_1_out15),
    .out16(demultiplexer_1_out16), .out17(demultiplexer_1_out17), .out18(demultiplexer_1_out18),
    .out19(demultiplexer_1_out19), .out20(demultiplexer_1_out20), .out21(demultiplexer_1_out21),
    .out22(demultiplexer_1_out22), .out23(demultiplexer_1_out23), .out24(demultiplexer_1_out24),
    .out25(demultiplexer_1_out25), .out26(demultiplexer_1_out26), .out27(demultiplexer_1_out27),
    .out28(demultiplexer_1_out28), .out29(demultiplexer_1_out29), .out30(demultiplexer_1_out30),
    .out31(demultiplexer_1_out31), .in(WD), .sel(A3), .en(in_3));  // open: out0
  // Probe on demultiplexer_1_out8
  Register #(.width(32)) u__0 (.D({32{1'b0}}), .Q(_0), .clk(in_1), .clr(in_2));  // open: en
  Register #(.width(32)) u__4 (.D(demultiplexer_1_out4), .Q(_4), .clk(in_1), .clr(in_2));  // open: en
  Register #(.width(32)) u__8 (.D(demultiplexer_1_out8), .Q(_8), .clk(in_1), .clr(in_2));  // open: en
  Register #(.width(32)) u__12 (.D(demultiplexer_1_out12), .Q(_12), .clk(in_1), .clr(in_2));  // open: en
  Register #(.width(32)) u__16 (.D(demultiplexer_1_out16), .Q(_16), .clk(in_1), .clr(in_2));  // open: en
  Register #(.width(32)) u__20 (.D(demultiplexer_1_out20), .Q(_20), .clk(in_1), .clr(in_2));  // open: en
  Register #(.width(32)) u__24 (.D(demultiplexer_1_out24), .Q(_24), .clk(in_1), .clr(in_2));  // open: en
  Register #(.width(32)) u__28 (.D(demultiplexer_1_out28), .Q(_28), .clk(in_1), .clr(in_2));  // open: en
  Register #(.width(32)) u__5 (.D(demultiplexer_1_out5), .Q(_5), .clk(in_1), .clr(in_2));  // open: en
  Register #(.width(32)) u__1 (.D(demultiplexer_1_out1), .Q(_1), .clk(in_1), .clr(in_2));  // open: en
  Register #(.width(32)) u__9 (.D(demultiplexer_1_out9), .Q(_9), .clk(in_1), .clr(in_2));  // open: en
  Register #(.width(32)) u__13 (.D(demultiplexer_1_out13), .Q(_13), .clk(in_1), .clr(in_2));  // open: en
  Register #(.width(32)) u__17 (.D(demultiplexer_1_out17), .Q(_17), .clk(in_1), .clr(in_2));  // open: en
  Register #(.width(32)) u__21 (.D(demultiplexer_1_out21), .Q(_21), .clk(in_1), .clr(in_2));  // open: en
  Register #(.width(32)) u__25 (.D(demultiplexer_1_out25), .Q(_25), .clk(in_1), .clr(in_2));  // open: en
  Register #(.width(32)) u__29 (.D(demultiplexer_1_out29), .Q(_29), .clk(in_1), .clr(in_2));  // open: en
  Register #(.width(32)) u__2 (.D(demultiplexer_1_out2), .Q(_2), .clk(in_1), .clr(in_2));  // open: en
  Register #(.width(32)) u__6 (.D(demultiplexer_1_out6), .Q(_6), .clk(in_1), .clr(in_2));  // open: en
  Register #(.width(32)) u__10 (.D(demultiplexer_1_out10), .Q(_10), .clk(in_1), .clr(in_2));  // open: en
  Register #(.width(32)) u__14 (.D(demultiplexer_1_out14), .Q(_14), .clk(in_1), .clr(in_2));  // open: en
  Register #(.width(32)) u__18 (.D(demultiplexer_1_out18), .Q(_18), .clk(in_1), .clr(in_2));  // open: en
  Register #(.width(32)) u__22 (.D(demultiplexer_1_out22), .Q(_22), .clk(in_1), .clr(in_2));  // open: en
  Register #(.width(32)) u__26 (.D(demultiplexer_1_out26), .Q(_26), .clk(in_1), .clr(in_2));  // open: en
  Register #(.width(32)) u__30 (.D(demultiplexer_1_out30), .Q(_30), .clk(in_1), .clr(in_2));  // open: en
  Register #(.width(32)) u__3 (.D(demultiplexer_1_out3), .Q(_3), .clk(in_1), .clr(in_2));  // open: en
  Register #(.width(32)) u__7 (.D(demultiplexer_1_out7), .Q(_7), .clk(in_1), .clr(in_2));  // open: en
  Register #(.width(32)) u__11 (.D(demultiplexer_1_out11), .Q(_11), .clk(in_1), .clr(in_2));  // open: en
  Register #(.width(32)) u__15 (.D(demultiplexer_1_out15), .Q(_15), .clk(in_1), .clr(in_2));  // open: en
  Register #(.width(32)) u__19 (.D(demultiplexer_1_out19), .Q(_19), .clk(in_1), .clr(in_2));  // open: en
  Register #(.width(32)) u__23 (.D(demultiplexer_1_out23), .Q(_23), .clk(in_1), .clr(in_2));  // open: en
  Register #(.width(32)) u__27 (.D(demultiplexer_1_out27), .Q(_27), .clk(in_1), .clr(in_2));  // open: en
  Register #(.width(32)) u__31 (.D(demultiplexer_1_out31), .Q(_31), .clk(in_1), .clr(in_2));  // open: en
  // Probe on _4
  Multiplexer #(.select(5), .width(32)) multiplexer_1 (
    .in0(_0), .in1(_1), .in2(_2), .in3(_3), .in4(_4), .in5(_5), .in6(_6), .in7(_7), .in8(_8), .in9(_9),
    .in10(_10), .in11(_11), .in12(_12), .in13(_13), .in14(_14), .in15(_15), .in16(_16), .in17(_17),
    .in18(_18), .in19(_19), .in20(_20), .in21(_21), .in22(_22), .in23(_23), .in24(_24), .in25(_25),
    .in26(_26), .in27(_27), .in28(_28), .in29(_29), .in30(_30), .in31(_31), .out(RD1), .sel(A1), .en(undriven));
  Multiplexer #(.select(5), .width(32)) multiplexer_2 (
    .in0(_0), .in1(_1), .in2(_2), .in3(_3), .in4(_4), .in5(_5), .in6(_6), .in7(_7), .in8(_8), .in9(_9),
    .in10(_10), .in11(_11), .in12(_12), .in13(_13), .in14(_14), .in15(_15), .in16(_16), .in17(_17),
    .in18(_18), .in19(_19), .in20(_20), .in21(_21), .in22(_22), .in23(_23), .in24(_24), .in25(_25),
    .in26(_26), .in27(_27), .in28(_28), .in29(_29), .in30(_30), .in31(_31), .out(RD2), .sel(A2));  // open: en

  // Other names for the same wires on the sheet: clk = in_1; reset = in_2; we = in_3
endmodule

module IFU (
  input  [31:0] RD1,
  input  [25:0] in_2,
  input  Zero,
  input  Branch,
  input  clk,
  input  JRSrc,
  input  JalSrc,
  input  reset,
  input  [31:0] SignImm,
  output [31:0] pc,
  output [31:0] Instr
);

  wire comparator_1_eq, PCSrc;
  wire [31:0] adder_1_out, adder_2_out, multiplexer_1_out, multiplexer_2_out, multiplexer_3_out,
       register_1_q, shifter_1_out, subtractor_1_out;

  Multiplexer #(.width(32)) multiplexer_1 (
    .in0(adder_1_out), .in1(adder_2_out), .out(multiplexer_1_out), .sel(PCSrc));  // open: en
  Multiplexer #(.width(32)) multiplexer_2 (
    .in0(multiplexer_1_out), .in1(RD1), .out(multiplexer_2_out), .sel(JRSrc));  // open: en
  and and_1 (PCSrc, Zero, Branch);
  Multiplexer #(.width(32)) multiplexer_3 (
    .in0(multiplexer_2_out), .in1({pc[31:28], in_2, 2'b00}), .out(multiplexer_3_out), .sel(JalSrc));  // open: en
  Register #(.width(32)) register_1 (.D(multiplexer_3_out), .Q(register_1_q), .clk(clk), .clr(reset));  // open: en
  Multiplexer #(.width(32)) multiplexer_4 (
    .in0(register_1_q), .in1(32'h3000), .out(pc), .sel(comparator_1_eq));  // open: en
  Comparator #(.width(32)) comparator_1 (.a(register_1_q), .b({32{1'b0}}), .eq(comparator_1_eq));  // open: gt, lt
  Adder #(.width(32)) adder_1 (.a(pc), .b(32'h4), .out(adder_1_out));  // open: cin, cout
  Shifter #(.width(32)) shifter_1 (.in(SignImm), .\dist (5'b00010), .out(shifter_1_out));
  Subtractor #(.width(32)) subtractor_1 (.a(pc), .b(32'h3000), .out(subtractor_1_out));  // open: bin, bout
  Adder #(.width(32)) adder_2 (.a(adder_1_out), .b(shifter_1_out), .out(adder_2_out));  // open: cin, cout
  ROM #(.addrWidth(12), .dataWidth(32)) rom_1 (.addr(subtractor_1_out[13:2]), .data(Instr));  // open: sel

  // Other names for the same wires on the sheet: Instr_Index[25:0] = in_2; instr_index_out[31:2] = {pc[31:28], in_2};
  //   rs_A1[31:0] = RD1

  // Notes on the sheet:
  //   PC
  //   IM
  //   contents of rom_1 (hex, n*v repeats v):
  //   3404007b 348501c8 3c06007b 3c07ffff 34e7ffff 868020 868020 868020 878820 e79020 10a4020 10a4020
  //   10a4020 34080000 ad040000 ad050004 ad060008 ad07000c ad100010 ad110014 ad120018 8d040000 8d05000c
  //   ad04001c ad050020 34040001 34050002 34060001 10850001 10860001 ad040024 ad050028
endmodule

module Splitter (
  input  [31:0] in_1,
  output [15:0] offset,
  output [25:0] InstrIndex,
  output [5:0] funct,
  output [4:0] shamt,
  output [4:0] A3,
  output [4:0] Rt_A2,
  output [4:0] Rs_A1,
  output [5:0] op
);

  // Probe on in_1

  assign A3 = in_1[15:11];
  assign funct = in_1[5:0];
  assign InstrIndex = in_1[25:0];
  assign offset = in_1[15:0];
  assign op = in_1[31:26];
  assign Rs_A1 = in_1[25:21];
  assign Rt_A2 = in_1[20:16];
  assign shamt = in_1[10:6];

  // Other names for the same wires on the sheet: Rt[4:0] = in_1[20:16]
endmodule

module Controller (
  input  [5:0] funct,
  input  [5:0] op,
  output out_3,
  output out_4,
  output out_5,
  output out_6,
  output out_7,
  output out_8,
  output out_9,
  output out_10,
  output jal,
  output [3:0] out_12
);

  wire add, beq, jal_t, jr, lui, lw, not_1_out, not_2_out, not_3_out, not_4_out, not_5_out, not_6_out,
       not_7_out, not_8_out, not_9_out, not_10_out, not_11_out, not_12_out, ori, sll, sub, sw;

  not not_1 (not_1_out, funct[2]);
  not not_2 (not_2_out, funct[3]);
  not not_3 (not_3_out, funct[4]);
  not not_4 (not_4_out, funct[5]);
  not not_5 (not_5_out, funct[0]);
  not not_6 (not_6_out, funct[1]);
  not not_7 (not_7_out, op[0]);
  not not_8 (not_8_out, op[1]);
  not not_9 (not_9_out, op[2]);
  not not_10 (not_10_out, op[3]);
  not not_11 (not_11_out, op[4]);
  not not_12 (not_12_out, op[5]);
  and u_add (add, funct[5], not_3_out, not_2_out, not_1_out, not_6_out, not_5_out, not_12_out, not_11_out, not_10_out, not_9_out, not_8_out, not_7_out);
  and u_sub (sub, funct[5], not_3_out, not_2_out, not_1_out, funct[1], not_5_out, not_12_out, not_11_out, not_10_out, not_9_out, not_8_out, not_7_out);
  and u_ori (ori, not_12_out, not_11_out, op[3], op[2], not_8_out, op[0]);
  and u_lw (lw, op[5], not_11_out, not_10_out, not_9_out, op[1], op[0]);
  and u_sw (sw, op[5], not_11_out, op[3], not_9_out, op[1], op[0]);
  and u_beq (beq, not_12_out, not_11_out, not_10_out, op[2], not_8_out, not_7_out);
  and u_lui (lui, not_12_out, not_11_out, op[3], op[2], op[1], op[0]);
  and u_sll (sll, not_4_out, not_3_out, not_2_out, not_1_out, not_6_out, not_5_out, not_12_out, not_11_out, not_10_out, not_9_out, not_8_out, not_7_out);
  and u_jr (jr, not_4_out, not_3_out, funct[3], not_1_out, not_6_out, not_5_out, not_12_out, not_11_out, not_10_out, not_9_out, not_8_out, not_7_out);
  and u_jal (jal_t, not_12_out, not_11_out, not_10_out, not_9_out, op[1], op[0]);
  or or_1 (out_3, add, sll, sub);
  or or_2 (out_4, ori, lw, sw, lui);
  buf or_3 (out_5, lw);  // OR_Gate
  or or_4 (out_6, sll, add, sub, ori, lw, lui, jal_t);
  buf or_5 (out_7, sw);  // OR_Gate
  buf or_6 (out_8, beq);  // OR_Gate
  or or_7 (out_9, lw, beq, sw);
  buf or_8 (out_10, jr);  // OR_Gate
  buf or_9 (jal, jal_t);  // OR_Gate
  buf or_10 (out_12[3], 1'b0);  // OR_Gate
  or or_11 (out_12[2], sll, 1'b0);
  or or_12 (out_12[1], ori, lui, 1'b0);
  or or_13 (out_12[0], sub, beq, 1'b0, lui, sll);

  // Other names for the same wires on the sheet: ALUSrc = out_4; Branch = out_8; ExtOp = out_9; JalSrc = jal;
  //   JRSrc = out_10; MemToReg = out_5; MemWrite = out_7; ALU_0 = out_12[0]; ALU_1 = out_12[1]; ALU_2 = out_12[2];
  //   ALU_3 = out_12[3]; RegDst = out_3; RegWrite = out_6
endmodule

module ALU (
  input  [3:0] in_1,
  input  [31:0] in_2,
  input  [31:0] in_3,
  input  [4:0] in_4,
  output [31:0] out_5,
  output Zero
);

  wire comparator_1_lt;
  wire [31:0] add, \and , lui, \or , sll, slt, sub, undriven, undriven_2, undriven_3;

  // Probe on in_2
  // Probe on in_3
  Adder #(.width(32)) adder_1 (.a(in_2), .b(in_3), .out(add));  // open: cin, cout
  Subtractor #(.width(32)) subtractor_1 (.a(in_2), .b(in_3), .out(sub));  // open: bin, bout
  assign \or  = in_2 | in_3;  // OR_Gate or_1, 32 bits wide
  Shifter #(.width(32)) shifter_1 (.in(in_3), .\dist (5'b10000), .out(lui));
  assign \and  = in_2 & in_3;  // AND_Gate and_1, 32 bits wide
  Shifter #(.width(32)) shifter_2 (.in(in_3), .\dist (in_4), .out(sll));
  Comparator #(.width(32)) comparator_1 (.a(in_2), .b(in_3), .lt(comparator_1_lt));  // open: gt, eq
  Multiplexer #(.width(32)) multiplexer_1 (
    .in0({32{1'b0}}), .in1(32'h1), .out(slt), .sel(comparator_1_lt));  // open: en
  Multiplexer #(.select(4), .width(32)) multiplexer_2 (
    .in0(add), .in1(sub), .in2(\or ), .in3(lui), .in4(\and ), .in5(sll), .in6(undriven_3), .in7(undriven_2),
    .in8(undriven), .out(out_5), .sel(in_1));  // open: in9, in10, in11, in12, in13, in14, in15, en
  Comparator #(.width(32)) comparator_2 (.a(out_5), .b({32{1'b0}}), .eq(Zero));  // open: gt, lt

  // Other names for the same wires on the sheet: ALUCtr[3:0] = in_1; Shamt[4:0] = in_4; SrcA[31:0] = in_2;
  //   SrcB[31:0] = in_3

  // Notes on the sheet:
  //   rs<rt?1:0
endmodule

module DM (
  input  [31:0] ALUResult,
  input  [31:0] WriteData,
  input  clk,
  input  reset,
  input  MemWrite,
  output [31:0] out_6
);

  RAM #(.addrWidth(12), .dataWidth(32), .bus("separate")) ram_1 (
    .addr(ALUResult[13:2]), .din(WriteData), .data(out_6), .str(MemWrite), .clk(clk), .clr(reset));  // open: sel, ld
  // NOT_Gate not_1 has open pins: in=MemWrite, out=open
endmodule

module EXT (
  input  [15:0] offset,
  input  ExtOp,
  output [31:0] SignImm
);

  wire [31:0] bit_extender_1_out, bit_extender_2_out;

  assign bit_extender_1_out = {{16{1'b0}}, offset};  // Bit_Extender bit_extender_1
  assign bit_extender_2_out = {{16{offset[15]}}, offset};  // Bit_Extender bit_extender_2
  Multiplexer #(.width(32)) multiplexer_1 (
    .in0(bit_extender_1_out), .in1(bit_extender_2_out), .out(SignImm), .sel(ExtOp));  // open: en
endmodule

module SrcBsel (
  input  [31:0] in_1,
  input  [31:0] in_2,
  input  in_3,
  output [31:0] out_4
);

  Multiplexer #(.width(32)) multiplexer_1 (.in0(in_1), .in1(in_2), .out(out_4), .sel(in_3));  // open: en
endmodule

module A3sel (
  input  [4:0] A2,
  input  [4:0] A3_in,
  input  Jalsrc,
  input  RegDst,
  output [4:0] add
);

  Multiplexer #(.select(2), .width(5)) multiplexer_1 (
    .in0(A2), .in1(A3_in), .in2({5{1'b1}}), .out(add), .sel({Jalsrc, RegDst}));  // open: in3, en
  // Probe on {Jalsrc, RegDst}
endmodule

module WD3sel (
  input  [31:0] ALUResult,
  input  [31:0] ReadData,
  input  [31:0] pc,
  input  JalSrc,
  input  MemToReg,
  output [31:0] regdata
);

  wire [31:0] adder_1_out;

  Adder #(.width(32)) adder_1 (.a(pc), .b(32'h4), .out(adder_1_out));  // open: cin, cout
  // Probe on {JalSrc, MemToReg}
  Multiplexer #(.select(2), .width(32), .disabled(0)) multiplexer_1 (
    .in0(ALUResult), .in1(ReadData), .in2(adder_1_out), .out(regdata), .sel({JalSrc, MemToReg}));  // open: in3, en
endmodule

module CMP (
  input  [31:0] in_1,
  input  [31:0] in_2,
  output out_3
);

  wire [31:0] and_1_out;

  assign and_1_out = in_1 & in_2;  // AND_Gate and_1, 32 bits wide
  Comparator #(.width(32)) comparator_1 (.a(and_1_out), .b({32{1'b0}}), .eq(out_3));  // open: gt, lt
endmodule
