// Logisim project Logisim_4BitSort.circ as structural Verilog: 3 circuits, main circuit 1bit_swap
module _1bit_swap (
  input  s,
  input  I1,
  input  I2,
  output O1,
  output O2
);

  wire and_1_out, and_2_out, and_3_out, and_4_out, not_1_out, not_2_out;

  not not_1 (not_1_out, s);
  not not_2 (not_2_out, s);
  and and_1 (and_1_out, not_1_out, I1);
  and and_2 (and_2_out, s, I2);
  and and_3 (and_3_out, not_2_out, I2);
  and and_4 (and_4_out, s, I1);
  or or_1 (O1, and_1_out, and_2_out);
  or or_2 (O2, and_3_out, and_4_out);
endmodule

module _4bit_swap (
  input  [3:0] A_in,
  input  OP,
  input  [3:0] B_in,
  output [3:0] A_out,
  output [3:0] B_out
);

  _1bit_swap _0 (.s(OP), .I1(A_in[0]), .I2(B_in[0]), .O1(A_out[0]), .O2(B_out[0]));
  _1bit_swap _1 (.s(OP), .I1(A_in[1]), .I2(B_in[1]), .O1(A_out[1]), .O2(B_out[1]));
  _1bit_swap _2 (.s(OP), .I1(A_in[2]), .I2(B_in[2]), .O1(A_out[2]), .O2(B_out[2]));
  _1bit_swap _3 (.s(OP), .I1(A_in[3]), .I2(B_in[3]), .O1(A_out[3]), .O2(B_out[3]));
endmodule

module _4bit_sort (
  input  [3:0] in_1,
  input  [3:0] in_2,
  input  [3:0] in_3,
  input  [3:0] in_4,
  output [3:0] out_5,
  output [3:0] out_6,
  output [3:0] out_7,
  output [3:0] out_8
);

  wire comparator_1_gt, comparator_2_gt, comparator_3_gt, comparator_4_gt, comparator_5_gt, comparator_6_gt;
  wire [3:0] n4bit_swap_1_a_out, n4bit_swap_1_b_out, n4bit_swap_2_a_out, n4bit_swap_2_b_out,
       n4bit_swap_3_a_out, n4bit_swap_3_b_out, n4bit_swap_4_b_out, n4bit_swap_5_b_out;

  Comparator #(.width(4), .mode("unsigned")) comparator_1 (.a(in_1), .b(in_2), .gt(comparator_1_gt));  // open: eq, lt
  _4bit_swap u_4bit_swap_1 (
    .OP(comparator_1_gt), .A_in(in_1), .A_out(n4bit_swap_1_a_out), .B_in(in_2), .B_out(n4bit_swap_1_b_out));
  Comparator #(.width(4), .mode("unsigned")) comparator_2 (
    .a(n4bit_swap_1_a_out), .b(in_3), .gt(comparator_2_gt));  // open: eq, lt
  _4bit_swap u_4bit_swap_2 (
    .OP(comparator_2_gt), .A_in(n4bit_swap_1_a_out), .A_out(n4bit_swap_2_a_out), .B_in(in_3),
    .B_out(n4bit_swap_2_b_out));
  Comparator #(.width(4), .mode("unsigned")) comparator_3 (
    .a(n4bit_swap_2_b_out), .b(n4bit_swap_1_b_out), .gt(comparator_3_gt));  // open: eq, lt
  _4bit_swap u_4bit_swap_3 (
    .OP(comparator_3_gt), .A_in(n4bit_swap_2_b_out), .A_out(n4bit_swap_3_a_out), .B_in(n4bit_swap_1_b_out),
    .B_out(n4bit_swap_3_b_out));
  Comparator #(.width(4), .mode("unsigned")) comparator_4 (
    .a(n4bit_swap_2_a_out), .b(in_4), .gt(comparator_4_gt));  // open: eq, lt
  _4bit_swap u_4bit_swap_4 (
    .OP(comparator_4_gt), .A_in(n4bit_swap_2_a_out), .A_out(out_5), .B_in(in_4), .B_out(n4bit_swap_4_b_out));
  Comparator #(.width(4), .mode("unsigned")) comparator_5 (
    .a(n4bit_swap_4_b_out), .b(n4bit_swap_3_a_out), .gt(comparator_5_gt));  // open: eq, lt
  _4bit_swap u_4bit_swap_5 (
    .OP(comparator_5_gt), .A_in(n4bit_swap_4_b_out), .A_out(out_6), .B_in(n4bit_swap_3_a_out),
    .B_out(n4bit_swap_5_b_out));
  Comparator #(.width(4), .mode("unsigned")) comparator_6 (
    .a(n4bit_swap_5_b_out), .b(n4bit_swap_3_b_out), .gt(comparator_6_gt));  // open: eq, lt
  _4bit_swap u_4bit_swap_6 (
    .OP(comparator_6_gt), .A_in(n4bit_swap_5_b_out), .A_out(out_7), .B_in(n4bit_swap_3_b_out), .B_out(out_8));
endmodule
