// Logisim project Logisim_fibonacci_1.circ as structural Verilog: 2 circuits, main circuit state_trans
module state_trans (
  input  [3:0] now,
  input  [3:0] pre,
  output [3:0] pre_new,
  output [3:0] now_new
);

  Adder #(.width(4)) adder_1 (.a(now), .b(pre), .out(now_new));  // open: cin, cout

  assign pre_new = now;
endmodule

module main (
  input  [2:0] in_1,
  output [3:0] out_2
);

  wire clock_1_out, comparator_1_eq, counter_1_q, counter_2_q, undriven, undriven_2, undriven_3, undriven_4,
       undriven_5, undriven_6;
  wire [3:0] adder_1_out, bit_extender_1_out, counter_3_q, multiplexer_1_out, multiplexer_2_out,
       register_1_q, register_2_q;

  Counter #(.width(1), .max('h1), .ongoal("stay")) counter_1 (
    .Q(counter_1_q), .clk(clock_1_out), .clr(undriven));  // open: load, D, count, carry
  Counter #(.width(1), .max('h1), .ongoal("stay")) counter_2 (
    .Q(counter_2_q), .clk(clock_1_out), .clr(undriven_2));  // open: load, D, count, carry
  Clock clock_1 (.out(clock_1_out));
  Multiplexer #(.width(4)) multiplexer_1 (
    .in0(4'b0000), .in1(register_1_q), .out(multiplexer_1_out), .sel(counter_1_q), .en(undriven_3));
  // Probe on register_2_q
  Multiplexer #(.width(4)) multiplexer_2 (
    .in0(4'b0001), .in1(register_2_q), .out(multiplexer_2_out), .sel(counter_2_q));  // open: en
  // Probe on multiplexer_2_out
  Adder #(.width(4)) adder_1 (.a(multiplexer_1_out), .b(multiplexer_2_out), .out(adder_1_out));  // open: cin, cout
  // Probe on adder_1_out
  assign bit_extender_1_out = {{1{1'b0}}, in_1};  // Bit_Extender bit_extender_1
  // Probe on register_1_q
  // Probe on bit_extender_1_out
  Counter #(.width(4), .max('hf)) counter_3 (
    .load(1'b0), .count(1'b1), .Q(counter_3_q), .clk(clock_1_out), .clr(undriven_4));  // open: D, carry
  Register #(.width(4)) register_1 (
    .D(multiplexer_2_out), .Q(register_1_q), .clk(clock_1_out), .clr(undriven_5));  // open: en
  Register #(.width(4)) register_2 (
    .D(adder_1_out), .Q(register_2_q), .clk(clock_1_out), .clr(undriven_6));  // open: en
  Clock clock_2 ();  // open: out
  Comparator #(.width(4)) comparator_1 (.a(bit_extender_1_out), .b(counter_3_q), .eq(comparator_1_eq));  // open: gt, lt
  Multiplexer #(.width(4)) multiplexer_3 (
    .in0(4'b0000), .in1(register_1_q), .out(out_2), .sel(comparator_1_eq));  // open: en
endmodule
