// Logisim project Logisim_mod5.circ as structural Verilog: 3 circuits, main circuit mod5
module mod5 (
  input  In,
  output s0,
  output s1,
  output s2,
  output s3,
  output s4
);

  wire clock_1_out;
  wire [1:0] register_1_q, state_transition_c_;

  state_transition state_transition (.c(register_1_q), .In(In), .c_(state_transition_c_));
  Register #(.width(2)) register_1 (.D(state_transition_c_), .Q(register_1_q), .clk(clock_1_out));  // open: en, clr
  Clock clock_1 (.out(clock_1_out));
  output_logic output_logic (.c(register_1_q), .In(In), .S0(s0), .S1(s1), .S2(s2), .S3(s3), .S4(s4));
endmodule

module state_transition (
  input  [1:0] c,
  input  In,
  output [1:0] c_
);


  assign c_ = {c[0], In};
endmodule

module output_logic (
  input  [1:0] c,
  input  In,
  output S0,
  output S1,
  output S2,
  output S3,
  output S4
);

  wire not_1_out, not_2_out, not_3_out, not_4_out;

  not not_1 (not_1_out, c[0]);
  not not_2 (not_2_out, In);
  not not_3 (not_3_out, c[0]);
  and and_1 (S3, c[0], In);
  not not_4 (not_4_out, In);
  and and_2 (S1, not_1_out, not_2_out);
  and and_3 (S2, not_3_out, In);
  and and_4 (S4, c[0], not_4_out);

  assign S0 = 1'b0;
endmodule
