// Logisim project swap.circ as structural Verilog: 1 circuit, main circuit swap
module swap (
  input  s,
  input  I1,
  input  I2,
  output O1,
  output O2
);

  wire and_1_out, and_2_out, and_3_out, and_4_out, not_1_out, not_2_out;

  not not_1 (not_1_out, s);
  not not_2 (not_2_out, s);
  and and_1 (and_1_out, not_1_out, I1);
  and and_2 (and_2_out, s, I2);
  and and_3 (and_3_out, not_2_out, I2);
  and and_4 (and_4_out, s, I1);
  or or_1 (O1, and_1_out, and_2_out);
  or or_2 (O2, and_3_out, and_4_out);
endmodule
